# Fritzing sketch duino-h-wiring (saved by Fritzing 0.9.3b)

parts:
  NodeMCU_V2 = NodeMCU V1.0
  OutputSwitch = Keyes Relay [package=THT]
  OutputSwitch_2 = Keyes Relay [package=THT]
  MotionInputSwitch = PIR sensor
  Buzzer = Piezo Speaker
  InputSwitch = Toggle Switch [package=THT]
  Display = OLED 0.96" 128x64 I2C SSD1306

nets:
  N1: NodeMCU_V2.D0, OutputSwitch.signal
  N2: NodeMCU_V2.D1, OutputSwitch_2.signal
  N3: NodeMCU_V2.D2, Display.SCL
  N4: NodeMCU_V2.D3, Display.SCA
  N5: NodeMCU_V2.D5, MotionInputSwitch.SIG
  N6: NodeMCU_V2.D6, InputSwitch.L1
  N7: NodeMCU_V2.D7, Buzzer.pin2

custom parts:
  NodeMCU V1.0: ESP8266 based NodeMCU
  Keyes Relay: The Keyes 5V relay module is suitable for SCM development, home appliance control. It uses a 5V~12V TIL control signal which can control DC / AC signal.
