# Fritzing sketch duino-k-wiring (saved by Fritzing 0.9.3b)

parts:
  NodeMCU_V2 = NodeMCU V1.0
  MatrixLed = 8x8 LED Modul mit MAX7219 [package=THT]
  FourDigitLed = Grove 4 Digit Display
  HygroThermoSensor = DHT11 Temperature & Humidity Sensor Module [package="Breakout board"]
  AnalogSensor = YL-83 Rain Sensor - Control Board
  R1 = Photocell (LDR) [package=THT]
  Buzzer = Piezo Speaker

nets:
  N1: NodeMCU_V2.D1, Buzzer.pin2
  N2: NodeMCU_V2.D2, FourDigitLed.CLK
  N3: NodeMCU_V2.D3, FourDigitLed.DIO
  N4: NodeMCU_V2.D5, MatrixLed.CLK_Eingang
  N5: NodeMCU_V2.D6, HygroThermoSensor.S
  N6: NodeMCU_V2.D7, MatrixLed.DIN_Eingang
  N7: NodeMCU_V2.D8, MatrixLed.CS_Eingang
  N8: NodeMCU_V2.A0, AnalogSensor.AO
  N9: AnalogSensor.POS, R1.pin_1
  N10: AnalogSensor.NEG, R1.pin_0

custom parts:
  NodeMCU V1.0: ESP8266 based NodeMCU
  DHT11 Temperature & Humidity Sensor Module: DHT11 temperature and humidity sensor module, provides a low-latency serial interface to measure humidity and temperature.
  YL-83 Rain Sensor - Control Board: The YL-83 is a rain sensor that has more resistance when dry and less resistance when wet. The module runs at 5V.
