# Fritzing sketch wiring (saved by Fritzing 0.9.3b)

parts:
  NodeMCU_V2 = NodeMCU V1.0
  8x8_Matrix_LED = 8x8 LED Modul mit MAX7219 [package=THT]
  4桁7セグメントディスプレイ = Grove 4 Digit Display
  湿温度センサー = DHT11 Temperature & Humidity Sensor Module [package="Breakout board"]
  人感センサースイッチ = RCWL-0516 Microwave Radar Motion Sensor Module
  IR送信 = KY-005 Infrared Transmitter Module [package="Breakout board"]
  リレースイッチ = Keyes Relay [package=THT]
  CdSセンサー = YL-83 Rain Sensor - Control Board
  R1 = PHOTOCELL [package=photocell-kit]

nets:
  N1: NodeMCU_V2.D0, リレースイッチ.signal
  N2: NodeMCU_V2.D1, 湿温度センサー.S
  N3: NodeMCU_V2.D2, 4桁7セグメントディスプレイ.CLK
  N4: NodeMCU_V2.D3, 4桁7セグメントディスプレイ.DIO
  N5: NodeMCU_V2.D4, 8x8_Matrix_LED.CS_Eingang
  N6: NodeMCU_V2.D5, 8x8_Matrix_LED.CLK_Eingang
  N7: NodeMCU_V2.D6, 人感センサースイッチ.OUT
  N8: NodeMCU_V2.D7, 8x8_Matrix_LED.DIN_Eingang
  N9: NodeMCU_V2.D8, IR送信.S
  N10: NodeMCU_V2.A0, CdSセンサー.AO
  N11: リレースイッチ.NC, リレースイッチ.C
  N12: CdSセンサー.POS, R1.P$2
  N13: CdSセンサー.NEG, R1.P$1

custom parts:
  NodeMCU V1.0: ESP8266 based NodeMCU
  DHT11 Temperature & Humidity Sensor Module: DHT11 temperature and humidity sensor module, provides a low-latency serial interface to measure humidity and temperature.
  RCWL-0516 Microwave Radar Motion Sensor Module: The RCWL-0516 is a microwave radar motion sensor module. Input voltage is 4V to 28V. The 3V3 pin is a power output.
  KY-005 Infrared Transmitter Module: Arduino IR Transmitter Module Keyes KY-005, emits infrared light at 38KHz.
  Keyes Relay: The Keyes 5V relay module is suitable for SCM development, home appliance control. It uses a 5V~12V TIL control signal which can control DC / AC signal.
  YL-83 Rain Sensor - Control Board: The YL-83 is a rain sensor that has more resistance when dry and less resistance when wet. The module runs at 5V.
